# Fritzing sketch bluetoot_sketch (saved by Fritzing 0.9.3b)
breadboards: 1

parts:
  Componente1 = Arduino Leonardo (Rev3b)
  Componente2 = Bluetooth HC-05 Macho
  LED1 = RGB LED (com. cathode, rbg) [package="5 mm [THT]"]
  R1 = Resistor [tolerance=±5% resistance=220 package="1206 [SMD]"]
  R2 = Resistor [tolerance=±5% resistance=220 package="1206 [SMD]"]
  R3 = Resistor [tolerance=±5% resistance=220 package="1206 [SMD]"]

nets:
  N1: Componente1.D0/RX, Componente2.TXD
  N2: Componente1.D5_PWM, R3.Pin_1
  N3: Componente1.D6_PWM/A7, R1.Pin_1
  5V: Componente1.5V, Componente2.VCC
  GND: Componente1.GND, Componente2.GND, LED1.common_cathode
  N4: Componente1.D9_PWM/A9, R2.Pin_1
  N5: LED1.red_anode, R3.Pin_0
  N6: LED1.blue_anode, R2.Pin_0
  N7: LED1.green_anode, R1.Pin_0
